# Fritzing sketch Wemos-RC522 (saved by Fritzing 0.9.3b)

parts:
  WeMos_D1_Mini1 = WeMos D1 Mini
  Onderdeel1 = RFID-RC522-v2

nets:
  3V3: WeMos_D1_Mini1.3V3, Onderdeel1.3.3V
  N1: WeMos_D1_Mini1.D4, Onderdeel1.RST
  N2: WeMos_D1_Mini1.D5, Onderdeel1.SCK
  N3: WeMos_D1_Mini1.D6, Onderdeel1.MISO
  N4: WeMos_D1_Mini1.D7, Onderdeel1.MOSI
  N5: WeMos_D1_Mini1.D8, Onderdeel1.SDA
  N6: WeMos_D1_Mini1.G, Onderdeel1.GND

custom parts:
  RFID-RC522-v2: A simple China made RFID-RC522 Reader; do check the pin labels, as this is a MFRC522 based clone.
